// Logisim project processor.circ as structural Verilog: 8 circuits, main circuit RegisterFile
module RegisterFile (
  input  [31:0] rd_data_in,
  input  [4:0] rs1_addr,
  input  [4:0] rs2_addr,
  input  [4:0] rd_addr,
  input  reg_write_en,
  input  clock,
  output [31:0] rs1_data,
  output [31:0] rs2_data
);

  wire w0, w1, w2, w3, w4, w5, w6, w7, w8, w9, w10, w11, w12, w13, w14, w15, w16, w17, w18, w19, w20, w21,
       w22, w23, w24, w25, w26, w27, w28, w29, w30, w31;
  wire [31:0] q0, q1, q2, q3, q4, q5, q6, q7, q8, q9, q10, q11, q12, q13, q14, q15, q16, q17, q18, q19, q20,
       q21, q22, q23, q24, q25, q26, q27, q28, q29, q30, q31;

  Multiplexer #(.select(5), .width(32)) multiplexer_1 (
    .in0(q0), .in1(q1), .in2(q2), .in3(q3), .in4(q4), .in5(q5), .in6(q6), .in7(q7), .in8(q8), .in9(q9),
    .in10(q10), .in11(q11), .in12(q12), .in13(q13), .in14(q14), .in15(q15), .in16(q16), .in17(q17),
    .in18(q18), .in19(q19), .in20(q20), .in21(q21), .in22(q22), .in23(q23), .in24(q24), .in25(q25),
    .in26(q26), .in27(q27), .in28(q28), .in29(q29), .in30(q30), .in31(q31), .out(rs1_data), .sel(rs1_addr));
  Demultiplexer #(.select(5)) demultiplexer_1 (
    .out0(w0), .out1(w1), .out2(w2), .out3(w3), .out4(w4), .out5(w5), .out6(w6), .out7(w7), .out8(w8),
    .out9(w9), .out10(w10), .out11(w11), .out12(w12), .out13(w13), .out14(w14), .out15(w15), .out16(w16),
    .out17(w17), .out18(w18), .out19(w19), .out20(w20), .out21(w21), .out22(w22), .out23(w23), .out24(w24),
    .out25(w25), .out26(w26), .out27(w27), .out28(w28), .out29(w29), .out30(w30), .out31(w31),
    .in(reg_write_en), .sel(rd_addr));
  Multiplexer #(.select(5), .width(32)) multiplexer_2 (
    .in0(q0), .in1(q1), .in2(q2), .in3(q3), .in4(q4), .in5(q5), .in6(q6), .in7(q7), .in8(q8), .in9(q9),
    .in10(q10), .in11(q11), .in12(q12), .in13(q13), .in14(q14), .in15(q15), .in16(q16), .in17(q17),
    .in18(q18), .in19(q19), .in20(q20), .in21(q21), .in22(q22), .in23(q23), .in24(q24), .in25(q25),
    .in26(q26), .in27(q27), .in28(q28), .in29(q29), .in30(q30), .in31(q31), .out(rs2_data), .sel(rs2_addr));
  Register #(.width(32)) register_1 (.D({32{1'b0}}), .en(w0), .clk(clock), .Q(q0));  // open: clr
  Register #(.width(32)) register_2 (.D(rd_data_in), .en(w4), .clk(clock), .Q(q4));  // open: clr
  Register #(.width(32)) register_3 (.D(rd_data_in), .en(w8), .clk(clock), .Q(q8));  // open: clr
  Register #(.width(32)) register_4 (.D(rd_data_in), .en(w12), .clk(clock), .Q(q12));  // open: clr
  Register #(.width(32)) register_5 (.D(rd_data_in), .en(w16), .clk(clock), .Q(q16));  // open: clr
  Register #(.width(32)) register_6 (.D(rd_data_in), .en(w20), .clk(clock), .Q(q20));  // open: clr
  Register #(.width(32)) register_7 (.D(rd_data_in), .en(w24), .clk(clock), .Q(q24));  // open: clr
  Register #(.width(32)) register_8 (.D(rd_data_in), .en(w28), .clk(clock), .Q(q28));  // open: clr
  Register #(.width(32)) register_9 (.D(rd_data_in), .en(w1), .clk(clock), .Q(q1));  // open: clr
  Register #(.width(32)) register_10 (.D(rd_data_in), .en(w5), .clk(clock), .Q(q5));  // open: clr
  Register #(.width(32)) register_11 (.D(rd_data_in), .en(w9), .clk(clock), .Q(q9));  // open: clr
  Register #(.width(32)) register_12 (.D(rd_data_in), .en(w13), .clk(clock), .Q(q13));  // open: clr
  Register #(.width(32)) register_13 (.D(rd_data_in), .en(w17), .clk(clock), .Q(q17));  // open: clr
  Register #(.width(32)) register_14 (.D(rd_data_in), .en(w21), .clk(clock), .Q(q21));  // open: clr
  Register #(.width(32)) register_15 (.D(rd_data_in), .en(w25), .clk(clock), .Q(q25));  // open: clr
  Register #(.width(32)) register_16 (.D(rd_data_in), .en(w29), .clk(clock), .Q(q29));  // open: clr
  Register #(.width(32)) register_17 (.D(rd_data_in), .en(w2), .clk(clock), .Q(q2));  // open: clr
  Register #(.width(32)) register_18 (.D(rd_data_in), .en(w6), .clk(clock), .Q(q6));  // open: clr
  Register #(.width(32)) register_19 (.D(rd_data_in), .en(w10), .clk(clock), .Q(q10));  // open: clr
  Register #(.width(32)) register_20 (.D(rd_data_in), .en(w14), .clk(clock), .Q(q14));  // open: clr
  Register #(.width(32)) register_21 (.D(rd_data_in), .en(w18), .clk(clock), .Q(q18));  // open: clr
  Register #(.width(32)) register_22 (.D(rd_data_in), .en(w22), .clk(clock), .Q(q22));  // open: clr
  Register #(.width(32)) register_23 (.D(rd_data_in), .en(w26), .clk(clock), .Q(q26));  // open: clr
  Register #(.width(32)) register_24 (.D(rd_data_in), .en(w30), .clk(clock), .Q(q30));  // open: clr
  Register #(.width(32)) register_25 (.D(rd_data_in), .en(w3), .clk(clock), .Q(q3));  // open: clr
  Register #(.width(32)) register_26 (.D(rd_data_in), .en(w7), .clk(clock), .Q(q7));  // open: clr
  Register #(.width(32)) register_27 (.D(rd_data_in), .en(w11), .clk(clock), .Q(q11));  // open: clr
  Register #(.width(32)) register_28 (.D(rd_data_in), .en(w15), .clk(clock), .Q(q15));  // open: clr
  Register #(.width(32)) register_29 (.D(rd_data_in), .en(w19), .clk(clock), .Q(q19));  // open: clr
  Register #(.width(32)) register_30 (.D(rd_data_in), .en(w23), .clk(clock), .Q(q23));  // open: clr
  Register #(.width(32)) register_31 (.D(rd_data_in), .en(w27), .clk(clock), .Q(q27));  // open: clr
  Register #(.width(32)) register_32 (.D(rd_data_in), .en(w31), .clk(clock), .Q(q31));  // open: clr

  // Other names for the same wires on the sheet: clk = clock
endmodule

module ByteAddrMemory (
  input  mem_write_en,
  input  [24:0] addr,
  input  [31:0] write_data,
  input  clock,
  output [31:0] read_data
);

  wire memorylogic_1_byte_0, memorylogic_1_byte_1, memorylogic_1_byte_2, memorylogic_1_byte_3;
  wire [7:0] multiplexer_1_out, ram_1_dout_2, ram_1_dout_3;
  wire [15:0] multiplexer_2_out, ram_1_dout;
  wire [31:0] bit_extender_1_out, bit_extender_2_out;

  MemoryLogic memorylogic_1 (
    .A(1'b1), .B(1'b0), .C(addr[1]), .D(addr[0]), .byte_0(memorylogic_1_byte_0),
    .byte_1(memorylogic_1_byte_1), .byte_2(memorylogic_1_byte_2), .byte_3(memorylogic_1_byte_3));
  RAM #(.addrWidth(23), .asyncread("true"), .byteenables("byteEnables"), .dataWidth(32), .\type ("nonvolatile")) ram_1 (
    .addr(addr[24:2]), .we(mem_write_en), .oe(1'b1), .clk(clock), .din(write_data),
    .dout({ram_1_dout, ram_1_dout_3, ram_1_dout_2}), .be3(memorylogic_1_byte_3), .be2(memorylogic_1_byte_2),
    .be1(memorylogic_1_byte_1), .be0(memorylogic_1_byte_0));
  Multiplexer #(.select(2), .width(8)) multiplexer_1 (
    .in0(ram_1_dout_2), .in1(ram_1_dout_3), .in2(ram_1_dout[7:0]), .in3(ram_1_dout[15:8]),
    .out(multiplexer_1_out), .sel(addr[1:0]));
  Multiplexer #(.width(16)) multiplexer_2 (
    .in0(ram_1_dout), .in1({ram_1_dout_3, ram_1_dout_2}), .out(multiplexer_2_out), .sel(addr[1]));
  assign bit_extender_1_out = {{24{multiplexer_1_out[7]}}, multiplexer_1_out};  // Bit_Extender bit_extender_1
  assign bit_extender_2_out = {{16{multiplexer_2_out[15]}}, multiplexer_2_out};  // Bit_Extender bit_extender_2
  Multiplexer #(.select(2), .width(32)) multiplexer_3 (
    .in0(bit_extender_1_out), .in1(bit_extender_2_out), .in2({ram_1_dout, ram_1_dout_3, ram_1_dout_2}),
    .out(read_data), .sel(2'b10));  // open: in3

  // Other names for the same wires on the sheet: ADDR_t[1:0] = addr[1:0]; D = addr[0]; C = addr[1]; clk = clock

  // Notes on the sheet:
  //   access hardwired to 2, always word access
endmodule

module MemoryLogic (
  input  A,
  input  B,
  input  C,
  input  D,
  output byte_0,
  output byte_1,
  output byte_2,
  output byte_3
);

  wire and_4_out, and_5_out, and_6_out, and_7_out, and_8_out, and_9_out, and_10_out, and_11_out, byte_access,
       half_access, not_1_out, not_2_out, not_3_out, not_4_out, word_access;

  not not_1 (not_1_out, C);
  not not_2 (not_2_out, B);
  not not_3 (not_3_out, A);
  not not_4 (not_4_out, D);
  and and_1 (word_access, A, not_2_out);
  and and_2 (half_access, B, not_3_out);
  and and_3 (byte_access, not_3_out, not_2_out);
  and and_4 (and_4_out, half_access, not_1_out);
  and and_5 (and_5_out, byte_access, not_1_out, not_4_out);
  and and_6 (and_6_out, half_access, not_1_out);
  and and_7 (and_7_out, byte_access, not_1_out, D);
  and and_8 (and_8_out, half_access, C);
  and and_9 (and_9_out, byte_access, C, not_4_out);
  and and_10 (and_10_out, half_access, C);
  and and_11 (and_11_out, byte_access, C, D);
  or or_1 (byte_0, word_access, and_4_out, and_5_out);
  or or_2 (byte_1, word_access, and_6_out, and_7_out);
  or or_3 (byte_2, word_access, and_8_out, and_9_out);
  or or_4 (byte_3, word_access, and_10_out, and_11_out);
endmodule

module ALU (
  input  [3:0] control,
  input  [31:0] A,
  input  [31:0] B,
  output zero_flag,
  output [31:0] ALU_out
);

  wire comparator_1_lt;
  wire [31:0] adder_1_out, and_1_out, bit_extender_1_out, or_1_out, subtractor_1_out, xor_1_out;

  assign and_1_out = A & B;  // AND_Gate and_1, 32 bits wide
  assign or_1_out = A | B;  // OR_Gate or_1, 32 bits wide
  assign xor_1_out = A ^ B;  // XOR_Gate xor_1, 32 bits wide
  Comparator #(.width(32)) comparator_1 (.a(A), .b(B), .lt(comparator_1_lt));  // open: gt, eq
  Adder #(.width(32)) adder_1 (.a(A), .b(B), .out(adder_1_out));  // open: cin, cout
  Subtractor #(.width(32)) subtractor_1 (.a(A), .b(B), .out(subtractor_1_out));  // open: bin, bout
  assign bit_extender_1_out = {{31{1'b0}}, comparator_1_lt};  // Bit_Extender bit_extender_1
  Multiplexer #(.select(4), .width(32)) multiplexer_1 (
    .in0(and_1_out), .in1(or_1_out), .in2(xor_1_out), .in3(bit_extender_1_out), .in8(adder_1_out),
    .in9(subtractor_1_out), .out(ALU_out), .sel(control));  // open: in4, in5, in6, in7, in10, in11, in12, in13, in14, in15
  Comparator #(.width(32)) comparator_2 (.a({32{1'b0}}), .b(ALU_out), .eq(zero_flag));  // open: gt, lt

  // Other names for the same wires on the sheet: alu_control[3:0] = control

  // Notes on the sheet:
  //   comes from ALU_Control
  //   and
  //   or
  //   add
  //   sub
  //   xor
  //   slt
endmodule

module ALU_Control (
  input  [1:0] ALU_op,
  input  [3:0] instruction,
  output [3:0] control_out
);

  wire and_1_out, and_2_out, and_3_out, and_4_out, and_5_out, and_6_out, comparator_1_eq, comparator_2_eq,
       comparator_3_eq, not_1_out, not_2_out, not_3_out, not_4_out, not_5_out, not_6_out, not_7_out,
       not_8_out, not_9_out, not_10_out, not_11_out, not_12_out, not_13_out, not_14_out, not_15_out,
       not_16_out;

  Comparator #(.width(2)) comparator_1 (.a(2'b00), .b(ALU_op), .eq(comparator_1_eq));  // open: gt, lt
  Comparator #(.width(2)) comparator_2 (.a(2'b01), .b(ALU_op), .eq(comparator_2_eq));  // open: gt, lt
  Comparator #(.width(2)) comparator_3 (.a(2'b10), .b(ALU_op), .eq(comparator_3_eq));  // open: gt, lt
  Multiplexer #(.width(4)) multiplexer_1 (.in1(4'b1000), .out(control_out), .sel(comparator_1_eq));  // open: in0
  Multiplexer #(.width(4)) multiplexer_2 (.in1(4'b1001), .out(control_out), .sel(comparator_2_eq));  // open: in0
  not not_1 (not_1_out, instruction[0]);
  not not_2 (not_2_out, instruction[1]);
  not not_3 (not_3_out, instruction[2]);
  not not_4 (not_4_out, instruction[3]);
  not not_5 (not_5_out, instruction[1]);
  not not_6 (not_6_out, instruction[2]);
  not not_7 (not_7_out, instruction[3]);
  not not_8 (not_8_out, instruction[0]);
  not not_9 (not_9_out, instruction[0]);
  not not_10 (not_10_out, instruction[3]);
  not not_11 (not_11_out, instruction[0]);
  not not_12 (not_12_out, instruction[2]);
  not not_13 (not_13_out, instruction[3]);
  not not_14 (not_14_out, instruction[0]);
  not not_15 (not_15_out, instruction[1]);
  not not_16 (not_16_out, instruction[3]);
  Multiplexer #(.width(4)) multiplexer_3 (.in1(4'b1000), .out(control_out), .sel(and_1_out));  // open: in0
  and and_1 (and_1_out, comparator_3_eq, not_1_out, not_2_out, not_3_out, not_4_out);
  Multiplexer #(.width(4)) multiplexer_4 (.in1(4'b1001), .out(control_out), .sel(and_2_out));  // open: in0
  and and_2 (and_2_out, comparator_3_eq, instruction[0], not_5_out, not_6_out, not_7_out);
  Multiplexer #(.width(4)) multiplexer_5 (.in1(4'b0000), .out(control_out), .sel(and_3_out));  // open: in0
  and and_3 (and_3_out, comparator_3_eq, not_8_out, instruction[1], instruction[2], instruction[3]);
  Multiplexer #(.width(4)) multiplexer_6 (.in1(4'b0001), .out(control_out), .sel(and_4_out));  // open: in0
  and and_4 (and_4_out, comparator_3_eq, not_9_out, instruction[1], instruction[2], not_10_out);
  Multiplexer #(.width(4)) multiplexer_7 (.in1(4'b0010), .out(control_out), .sel(and_5_out));  // open: in0
  and and_5 (and_5_out, comparator_3_eq, not_11_out, instruction[1], not_12_out, not_13_out);
  Multiplexer #(.width(4)) multiplexer_8 (.in1(4'b0011), .out(control_out), .sel(and_6_out));  // open: in0
  and and_6 (and_6_out, comparator_3_eq, not_14_out, not_15_out, instruction[2], not_16_out);

  // Other names for the same wires on the sheet: control[3:0] = control_out

  // Notes on the sheet:
  //   comes from
  //   control unit
  //   add (lw and sw)
  //   sub (branch)
  //   anything else
  //   goes into ALU
  //   bits 1-3: funct3
  //   bit 0: funct7
  //   flipped, read backwards
  //   add
  //   sub
  //   and
  //   or
  //   xor
  //   slt
endmodule

module ImmediateGen (
  input  [31:0] Input,
  input  [1:0] ImmSel,
  output [31:0] immediate
);

  wire [31:0] bit_extender_1_out, bit_extender_2_out, bit_extender_3_out, bit_extender_4_out;

  assign bit_extender_1_out = {{20{Input[31]}}, Input[31:20]};  // Bit_Extender bit_extender_1
  assign bit_extender_2_out = {{20{Input[31]}}, {Input[31:25], Input[11:7]}};  // Bit_Extender bit_extender_2
  assign bit_extender_3_out = {{19{Input[31]}}, {Input[31], Input[7], Input[30:25], Input[11:8], 1'b0}};  // Bit_Extender bit_extender_3
  assign bit_extender_4_out = {{11{Input[31]}}, {Input[31], Input[19:12], Input[20], Input[30:21], 1'b0}};  // Bit_Extender bit_extender_4
  Multiplexer #(.enable("true"), .select(2), .width(32)) multiplexer_1 (
    .in0(bit_extender_1_out), .in1(bit_extender_2_out), .in2(bit_extender_3_out), .in3(bit_extender_4_out),
    .out(immediate), .sel(ImmSel));  // open: en

  // Notes on the sheet:
  //   J-Type immediate
  //   I-Type immediate
  //   S-Type immediate
  //   B-Type immediate
  //   Itype tested and works 
endmodule

module ControlUnit (
  input  [6:0] OPcode,
  output [1:0] ALUop,
  output [1:0] ImmSel,
  output Jump,
  output Branch,
  output [1:0] WBsel,
  output Write,
  output Read,
  output ALUsrc,
  output RegWrite
);

  wire comparator_1_eq, comparator_2_eq, comparator_3_eq, comparator_4_eq, comparator_5_eq, comparator_6_eq;
  wire [2:0] priority_encoder_1_out;
  wire [11:0] multiplexer_1_out, multiplexer_2_out, multiplexer_3_out, multiplexer_5_out, multiplexer_6_out,
       multiplexer_7_out;

  Comparator #(.width(7)) comparator_1 (.a(OPcode), .b(7'b0010011), .eq(comparator_1_eq));  // open: gt, lt
  Multiplexer #(.enable("true"), .width(12)) multiplexer_1 (
    .in1(12'hc02), .out(multiplexer_1_out), .sel(comparator_1_eq));  // open: in0, en
  Comparator #(.width(7)) comparator_2 (.a(OPcode), .b(7'b0110011), .eq(comparator_2_eq));  // open: gt, lt
  Multiplexer #(.enable("true"), .width(12)) multiplexer_2 (
    .in1(12'h802), .out(multiplexer_2_out), .sel(comparator_2_eq));  // open: in0, en
  Comparator #(.width(7)) comparator_3 (.a(OPcode), .b(7'b0100011), .eq(comparator_3_eq));  // open: gt, lt
  Comparator #(.width(7)) comparator_4 (.a(OPcode), .b(7'b0000011), .eq(comparator_4_eq));  // open: gt, lt
  Multiplexer #(.enable("true"), .width(12)) multiplexer_3 (
    .in1(12'h504), .out(multiplexer_3_out), .sel(comparator_3_eq));  // open: in0, en
  Multiplexer #(.enable("true"), .select(3), .width(12)) multiplexer_4 (
    .in0(multiplexer_1_out), .in1(multiplexer_2_out), .in2(multiplexer_3_out), .in3(multiplexer_5_out),
    .in4(multiplexer_6_out), .in5(multiplexer_7_out),
    .out({RegWrite, ALUsrc, Read, Write, WBsel, Branch, Jump, ImmSel, ALUop}), .sel(priority_encoder_1_out));  // open: in6, in7, en
  Multiplexer #(.enable("true"), .width(12)) multiplexer_5 (
    .in1(12'he40), .out(multiplexer_5_out), .sel(comparator_4_eq));  // open: in0, en
  Comparator #(.width(7)) comparator_5 (.a(OPcode), .b(7'b1101111), .eq(comparator_5_eq));  // open: gt, lt
  Multiplexer #(.enable("true"), .width(12)) multiplexer_6 (
    .in1(12'h89c), .out(multiplexer_6_out), .sel(comparator_5_eq));  // open: in0, en
  Comparator #(.width(7)) comparator_6 (.a(OPcode), .b(7'b1100011), .eq(comparator_6_eq));  // open: gt, lt
  Multiplexer #(.enable("true"), .width(12)) multiplexer_7 (
    .in1(12'h429), .out(multiplexer_7_out), .sel(comparator_6_eq));  // open: in0, en
  Priority_Encoder priority_encoder_1 (
    .in0(comparator_1_eq), .in1(comparator_2_eq), .in2(comparator_3_eq), .in3(comparator_4_eq),
    .in4(comparator_5_eq), .in5(comparator_6_eq), .out(priority_encoder_1_out));  // open: in6, in7, en_in, gs, en_out

  // Notes on the sheet:
  //   I-op
  //   R-op
  //   Store
  //   Load
  //   Jump
  //   Branch
endmodule

module Datapath (
  output [3:0] out_1,
  output [31:0] write_data,
  output [1:0] WBSel,
  output [3:0] ALUcontrol,
  output [1:0] ImmSel,
  output [1:0] ALUop,
  output zero_flag,
  output [31:0] rd_data_in,
  output [31:0] out_9
);

  wire ALUsrc, and_1_out, and_2_out, Branch, clk, Jump, not_1_out, not_2_out, or_1_out, Read, Register_Write,
       Write;
  wire [4:0] rd_addr, rs1_addr, rs2_addr;
  wire [6:0] opcode;
  wire [23:0] PC_q;
  wire [24:0] addr;
  wire [31:0] alu_2_alu_out, byteaddrmemory_1_read_data, immediate, multiplexer_2_out, PC4, PC_out,
       registerfile_1_rs1_data;
  wire [31:25] alu_3_alu_out, InstructionMemory_data;

  Register #(.width(24)) PC (.D(out_9[23:0]), .clk(clk), .Q(PC_q));  // open: en, clr
  ROM #(.addrWidth(24), .dataWidth(32)) InstructionMemory (
    .addr(PC_q),
    .data({InstructionMemory_data[31], out_1[0], InstructionMemory_data[29:25], rs2_addr, rs1_addr, out_1[1], out_1[2], out_1[3], rd_addr, opcode}));
  assign PC_out = {{8{1'b0}}, PC_q};  // Bit_Extender bit_extender_1
  ImmediateGen immediategen_1 (
    .Input({InstructionMemory_data[31], out_1[0], InstructionMemory_data[29:25], rs2_addr, rs1_addr, out_1[1], out_1[2], out_1[3], rd_addr, opcode}),
    .ImmSel(ImmSel), .immediate(immediate));
  Clock clock_1 (.out(clk));
  ControlUnit controlunit_1 (
    .OPcode(opcode), .ALUop(ALUop), .ImmSel(ImmSel), .Jump(Jump), .Branch(Branch), .WBsel(WBSel),
    .Write(Write), .Read(Read), .ALUsrc(ALUsrc), .RegWrite(Register_Write));
  ALU_Control alu_control_1 (.ALU_op(ALUop), .instruction(out_1), .control_out(ALUcontrol));
  ALU alu_1 (.control(4'b1000), .A(PC_out), .B(32'h4), .ALU_out(PC4));  // open: zero_flag
  ALU alu_2 (.control(4'b1000), .A(PC_out), .B(immediate), .ALU_out(alu_2_alu_out));  // open: zero_flag
  not not_1 (not_1_out, out_1[3]);
  and and_1 (and_1_out, Branch, not_1_out, not_2_out);
  not not_2 (not_2_out, zero_flag);
  and and_2 (and_2_out, zero_flag, out_1[3], Branch);
  Multiplexer #(.width(32)) multiplexer_1 (.in0(PC4), .in1(alu_2_alu_out), .out(out_9), .sel(or_1_out));
  or or_1 (or_1_out, and_1_out, and_2_out, Jump);
  RegisterFile registerfile_1 (
    .rd_data_in(rd_data_in), .rs1_addr(rs1_addr), .rs2_addr(rs2_addr), .rd_addr(rd_addr),
    .reg_write_en(Register_Write), .clock(clk), .rs1_data(registerfile_1_rs1_data), .rs2_data(write_data));
  Multiplexer #(.width(32)) multiplexer_2 (.in0(write_data), .in1(immediate), .out(multiplexer_2_out), .sel(ALUsrc));
  ALU alu_3 (
    .control(ALUcontrol), .A(registerfile_1_rs1_data), .B(multiplexer_2_out), .zero_flag(zero_flag),
    .ALU_out({alu_3_alu_out, addr}));
  ByteAddrMemory byteaddrmemory_1 (
    .mem_write_en(Write), .addr(addr), .write_data(write_data), .clock(clk),
    .read_data(byteaddrmemory_1_read_data));
  Multiplexer #(.select(2), .width(32)) multiplexer_3 (
    .in0({alu_3_alu_out, addr}), .in1(byteaddrmemory_1_read_data), .in2(PC4), .out(rd_data_in), .sel(WBSel));  // open: in3

  // Other names for the same wires on the sheet: PC_in[31:0] = out_9; instruction[3:0] = out_1; branchType = out_1[3]

  // Notes on the sheet:
  //   contents of InstructionMemory (hex, n*v repeats v):
  //   500093 0 0 0 500113 0 0 0 208463 0 0 0 6f00193 0 0 0 de00193 0 0 0 209663 0 0 0 700213 0 0 0 8002ef
  //   0 0 0 900313 0 0 0 a00313
  //   Immediate Generator
  //   Instruction bits 30 and 12-14
  //   flipped! read backwards!
  //   instruction bits 20-24
  //   opcode bits 0-6
  //   instruction bits 7-11
  //   instruction bits 15-19
endmodule
